// Logisim project GivenCache.circ as structural Verilog: 8 circuits, main circuit main
module main (
  input  EnableTestHalting,
  output [9:0] CorrectCounter,
  output [9:0] HitCounter,
  output [9:0] MissCounter,
  output [9:0] TestNumber,
  output [7:0] ByteRead,
  output [7:0] CorrectByteRead,
  output Halt
);

  wire and_3_out, and_4_out, and_5_out, CLK, CmdIsRead, Correct, CpuRead, CpuWrite, DidContain, HaltTesting,
       MaxItersReached, MemRead, MemWrite, not_1_out, not_2_out, not_4_out, NotDoneTesting, Ok2Count,
       or_1_out, Ready;
  wire [7:0] CpuWriteValue, MemAddress;
  wire [9:0] CpuAddress;
  wire [31:0] Line2Mem, LineFromMem;

  not not_1 (not_1_out, Ready);
  Clock clock_1 (.out(CLK));
  or or_1 (or_1_out, MaxItersReached, Ready);
  Counter #(.width(4), .max('h9)) MaxClocks (
    .load(Ready), .D(4'b0001), .count(not_1_out), .carry(MaxItersReached), .clk(CLK));  // open: Q, clr
  and and_1 (HaltTesting, EnableTestHalting, CmdIsRead, not_2_out);
  not not_2 (not_2_out, Correct);
  not not_3 (NotDoneTesting, Halt);
  Inputs inputs_1 (
    .HaltTesting(HaltTesting), .Ready(or_1_out), .CLK(CLK), .Done(Halt), .Read(CpuRead), .Write(CpuWrite),
    .Address(CpuAddress), .Value(CpuWriteValue), .TestNumber(TestNumber));
  Cache cache_1 (
    .CpuAddress(CpuAddress), .CpuRead(CpuRead), .CpuWrite(CpuWrite), .CpuWriteValue(CpuWriteValue),
    .CLK(CLK), .Ready(Ready), .DidContain(DidContain), .ByteRead(ByteRead), .MemAddress(MemAddress),
    .MemRead(MemRead), .MemWrite(MemWrite), .LineFromMem(LineFromMem), .Line2Mem(Line2Mem));
  // Probe on CpuRead
  // Probe on CpuWrite
  // Probe on CpuAddress
  // Probe on CpuWriteValue
  // Probe on TestNumber
  // Probe on CorrectByteRead
  // Probe on Correct
  // Probe on Ready
  // Probe on DidContain
  // Probe on ByteRead
  // Probe on MemAddress
  // Probe on MemRead
  // Probe on MemWrite
  // Probe on HitCounter
  // Probe on LineFromMem
  // Probe on Line2Mem
  not not_4 (not_4_out, HaltTesting);
  RAM #(.dataWidth(32), .bus("separate")) ram_1 (
    .addr(MemAddress), .din(Line2Mem), .data(LineFromMem), .str(MemWrite), .clk(CLK), .ld(MemRead));  // open: sel, clr
  and and_2 (Ok2Count, Ready, not_4_out, NotDoneTesting);
  // Probe on LineFromMem
  and and_3 (and_3_out, Correct, Ok2Count);
  and and_4 (and_4_out, DidContain, Ok2Count);
  and and_5 (and_5_out, MemRead, NotDoneTesting);
  // Probe on TestNumber
  Checker checker_1 (
    .TestNumber(TestNumber), .YourByteRead(ByteRead), .CmdIsRead(CmdIsRead),
    .CorrectByteRead(CorrectByteRead), .Correct(Correct));
  // Probe on ByteRead
  Counter #(.width(10), .max('h3ff)) u_CorrectCounter (
    .count(and_3_out), .Q(CorrectCounter), .clk(CLK));  // open: load, D, carry, clr
  Counter #(.width(10), .max('h3ff)) u_HitCounter (
    .count(and_4_out), .Q(HitCounter), .clk(CLK));  // open: load, D, carry, clr
  Counter #(.width(10), .max('h3ff)) u_MissCounter (
    .count(and_5_out), .Q(MissCounter), .clk(CLK));  // open: load, D, carry, clr
  // Probe on CorrectByteRead
  // Probe on CorrectCounter
  // Probe on HitCounter
  // Probe on MissCounter

  // Other names for the same wires on the sheet: DoneTesting = Halt

  // Notes on the sheet:
  //   Your Answer Inside Here
  //   Mathew Magno 913366789
  //   Muhammed Waheed 912741428
endmodule

module Cache (
  input  [9:0] CpuAddress,
  input  CpuRead,
  input  CpuWrite,
  input  [7:0] CpuWriteValue,
  input  CLK,
  input  [31:0] LineFromMem,
  output Ready,
  output DidContain,
  output [7:0] ByteRead,
  output [7:0] MemAddress,
  output MemRead,
  output MemWrite,
  output [31:0] Line2Mem
);

  wire ByteWriteFlag, ByteWriteFlag0, ByteWriteFlag1, DidContain0, DidContain1, DidContainBuffer, Dirty0,
       dirty0_t, Dirty1, dirty1_t, DirtyFlag, init, MemRead0, MemRead1, multiplexer_5_out, multiplexer_6_out,
       or_1_out, SaveInputs, SaveInputsOnReady, setDirty, StoredRead, StoredWrite, updateAge, updateAge0,
       updateAge1, valid, valid0, valid1;
  wire [6:0] Tag0, Tag1;
  wire [7:0] Data0, Data1, WriteValue;
  wire [7:1] memAddressWrite;
  wire [9:0] Address;
  wire [31:0] line2Mem0, line2Mem1;

  // Probe on CpuAddress
  // Probe on CpuAddress
  or or_1 (or_1_out, CpuWrite, CpuRead);
  Register State (.D(CpuWriteValue), .en(SaveInputsOnReady), .Q(WriteValue), .clk(CLK));  // open: clr
  Register #(.width(1)) State_2 (.D(CpuRead), .en(SaveInputsOnReady), .Q(StoredRead), .clk(CLK));  // open: clr
  // Probe on StoredWrite
  Register #(.width(1)) State_3 (.D(CpuWrite), .en(SaveInputsOnReady), .Q(StoredWrite), .clk(CLK));  // open: clr
  // Probe on Address
  Register #(.width(10)) State_4 (.D(CpuAddress), .en(SaveInputsOnReady), .Q(Address), .clk(CLK));  // open: clr
  // Probe on CpuWriteValue
  // Probe on Address
  and and_1 (SaveInputsOnReady, Ready, or_1_out);
  // Probe on Address[1:0]
  // Probe on Address[2]
  // Probe on Address[9:3]
  Multiplexer #(.enable("false")) multiplexer_1 (.in0(dirty0_t), .in1(dirty1_t), .out(DirtyFlag), .sel(Address[2]));
  Set Set0 (
    .Tag(Address[9:3]), .clk(CLK), .offset(Address[1:0]), .Setvalid(valid0), .contains(DidContain0),
    .Data(WriteValue), .init(init), .dirty(dirty0_t), .Data_2(Data0), .updateAge(updateAge0),
    .SetDirty(Dirty0), .lineBlocks(line2Mem0), .TagOut(Tag0), .MemLine(LineFromMem), .memRead(MemRead0),
    .ByteWrite(ByteWriteFlag0));
  Demultiplexer #(.enable("false")) demultiplexer_1 (.out0(MemRead0), .out1(MemRead1), .in(MemRead), .sel(Address[2]));
  // Probe on setDirty
  Demultiplexer #(.enable("false")) demultiplexer_2 (.out0(Dirty0), .out1(Dirty1), .in(setDirty), .sel(Address[2]));
  // Probe on Address[2]
  Demultiplexer #(.enable("false")) demultiplexer_3 (
    .out0(updateAge0), .out1(updateAge1), .in(updateAge), .sel(Address[2]));
  // Probe on Dirty0
  // Probe on Dirty1
  Multiplexer #(.enable("false")) multiplexer_2 (
    .in0(DidContain0), .in1(DidContain1), .out(DidContainBuffer), .sel(Address[2]));
  // Probe on ByteWriteFlag
  Demultiplexer #(.enable("false")) demultiplexer_4 (
    .out0(ByteWriteFlag0), .out1(ByteWriteFlag1), .in(ByteWriteFlag), .sel(Address[2]));
  Register #(.width(1)) State_5 (.D(DidContainBuffer), .en(SaveInputs), .Q(DidContain), .clk(CLK));  // open: clr
  Set Set1 (
    .Tag(Address[9:3]), .clk(CLK), .offset(Address[1:0]), .Setvalid(valid1), .contains(DidContain1),
    .Data(WriteValue), .init(init), .dirty(dirty1_t), .Data_2(Data1), .updateAge(updateAge1),
    .SetDirty(Dirty1), .lineBlocks(line2Mem1), .TagOut(Tag1), .MemLine(LineFromMem), .memRead(MemRead1),
    .ByteWrite(ByteWriteFlag1));
  Demultiplexer #(.enable("false")) demultiplexer_5 (.out0(valid0), .out1(valid1), .in(valid), .sel(Address[2]));
  // Probe on LineFromMem
  // Probe on LineFromMem
  // Probe on Tag0
  Multiplexer #(.width(7), .enable("false")) multiplexer_3 (
    .in0(Tag0), .in1(Tag1), .out(memAddressWrite), .sel(Address[2]));
  Multiplexer #(.width(8), .enable("false")) multiplexer_4 (.in0(Data0), .in1(Data1), .out(ByteRead), .sel(Address[2]));
  // Probe on ByteRead
  Multiplexer #(.enable("false")) multiplexer_5 (.in0(StoredRead), .in1(CpuRead), .out(multiplexer_5_out), .sel(Ready));
  Multiplexer #(.enable("false")) multiplexer_6 (
    .in0(StoredWrite), .in1(CpuWrite), .out(multiplexer_6_out), .sel(Ready));
  // Probe on {memAddressWrite, Address[2]}
  // Probe on {memAddressWrite, Address[2]}
  // Probe on Address[9:3]
  fsm_controls FSM (
    .read(multiplexer_5_out), .write(multiplexer_6_out), .contains(DidContainBuffer), .dirty(DirtyFlag),
    .ready(Ready), .setDirty(setDirty), .valid(valid), .UpdateAge(updateAge), .memRead(MemRead),
    .memWrite(MemWrite), .byteWrite(ByteWriteFlag), .init(init), .SaveInputs(SaveInputs), .CLK(CLK));
  // Probe on Address[9:2]
  // Probe on Address[9:2]
  Multiplexer #(.width(8), .enable("false")) multiplexer_7 (
    .in0(Address[9:2]), .in1({memAddressWrite, Address[2]}), .out(MemAddress), .sel(MemWrite));
  // Probe on MemAddress
  Multiplexer #(.width(32), .enable("false")) multiplexer_8 (
    .in0(line2Mem0), .in1(line2Mem1), .out(Line2Mem), .sel(Address[2]));
  // Probe on Line2Mem
  // Probe on LineFromMem[7:0]
  // Probe on LineFromMem[15:8]
  // Probe on LineFromMem[23:16]
  // Probe on LineFromMem[31:24]
  // Probe on LineFromMem
  // Probe on LineFromMem
  // Probe on ByteRead
  // Probe on MemAddress
  // Probe on MemAddress
  // Probe on Line2Mem
  // Probe on Line2Mem

  // Other names for the same wires on the sheet: offset[1:0] = Address[1:0]; LineFromMemBuffer[31:0] = LineFromMem;
  //   memAddressRead[7:0] = Address[9:2]; memAddressWrite[0] = Address[2]; SetNum = Address[2];
  //   TAG[6:0] = Address[9:3]

  // Notes on the sheet:
  //   Address Bits = 10
  //   Line Size = 4
  //   W = 3
  //   Num Sets = 2
  //   C =4*3*2 = 24bytes
  //   Tag bits = 7
endmodule

module Inputs (
  input  HaltTesting,
  input  Ready,
  input  CLK,
  output Done,
  output Read,
  output Write,
  output [9:0] Address,
  output [7:0] Value,
  output [9:0] TestNumber
);

  wire and_1_out, not_1_out, not_2_out;

  not not_1 (not_1_out, HaltTesting);
  not not_2 (not_2_out, Done);
  Counter #(.width(10), .max('h3ff), .ongoal("stay")) u_TestNumber (
    .count(and_1_out), .Q(TestNumber), .clk(CLK));  // open: load, D, carry, clr
  and and_1 (and_1_out, not_1_out, Ready, not_2_out);
  ROM #(.addrWidth(10), .dataWidth(21)) rom_1 (
    .addr(TestNumber), .data({Done, Read, Write, Address, Value}));  // open: sel

  // Notes on the sheet:
  //   contents of rom_1 (hex, n*v repeats v):
  //   40005 40106 40207 40308 40409 4050a 4060b 4070c 4080d 4090e 40a0f 40b10 40c11 40d12 40e13 40f14
  //   41015 41116 41217 41318 41419 4151a 4161b 4171c 80000 81000 81000 82000 82000 83000 80400 81400
  //   81400 82400 82400 83400 80000 80100 80200 80300 80400 80500 80600 80700 80800 80900 80a00 80b00
  //   80c00 80d00 80e00 80f00 81000 81100 81200 81300 81400 81500 81600 81700 0 100000
endmodule

module Checker (
  input  [9:0] TestNumber,
  input  [7:0] YourByteRead,
  output CmdIsRead,
  output [7:0] CorrectByteRead,
  output Correct
);

  wire comparator_1_eq;
  wire [9:0] subtractor_1_out;

  // Probe on TestNumber
  Subtractor #(.width(10)) subtractor_1 (.a(TestNumber), .b(10'h1), .out(subtractor_1_out));  // open: bin, bout
  ROM #(.addrWidth(10), .dataWidth(9)) rom_1 (
    .addr(subtractor_1_out), .data({CmdIsRead, CorrectByteRead}));  // open: sel
  Comparator #(.mode("unsigned")) comparator_1 (
    .a(YourByteRead), .b(CorrectByteRead), .eq(comparator_1_eq));  // open: gt, lt
  and and_1 (Correct, comparator_1_eq, CmdIsRead);

  // Other names for the same wires on the sheet: Test_Number[9:0] = TestNumber

  // Notes on the sheet:
  //   Read Solutions
  //   contents of rom_1 (hex, n*v repeats v):
  //   5 6 7 8 9 a b c d e f 10 11 12 13 14 15 16 17 18 19 1a 1b 1c 105 115 115 120 120 130 109 119 119 124
  //   124 134 105 106 107 108 109 10a 10b 10c 10d 10e 10f 110 111 112 113 114 115 116 117 118 119 11a 11b
  //   11c
endmodule

module Line (
  input  [6:0] setTag,
  input  setDirty,
  input  UpdateAge,
  input  setValid,
  input  [1:0] offset,
  input  CLK,
  input  [7:0] SetData,
  input  [1:0] SetAge,
  input  init,
  input  memRead,
  input  [31:0] Mem,
  input  Write2Cache,
  input  [1:0] SelectedAge,
  output [31:0] IineBlocks,
  output [7:0] Block,
  output dirty,
  output valid,
  output [1:0] Age,
  output [6:0] Tag
);

  wire not_1_out, not_2_out, not_3_out, not_4_out, or_1_out, or_2_out, or_3_out, or_4_out, or_5_out,
       or_6_out, or_7_out, WriteEnable0, WriteEnable1, WriteEnable2, WriteEnable3;
  wire [1:0] updateage_1_nextage;
  wire [7:0] multiplexer_1_out, multiplexer_2_out, multiplexer_3_out, multiplexer_4_out;

  // Probe on offset
  // Probe on SetData
  // Probe on Mem[7:0]
  // Probe on Mem[15:8]
  not not_1 (not_1_out, memRead);
  not not_2 (not_2_out, memRead);
  // Probe on Mem
  not not_3 (not_3_out, memRead);
  // Probe on SetData
  or or_1 (or_1_out, WriteEnable0, memRead);
  Multiplexer #(.width(8), .enable("false")) multiplexer_1 (
    .in0(Mem[23:16]), .in1(SetData), .out(multiplexer_1_out), .sel(not_1_out));
  or or_2 (or_2_out, WriteEnable2, memRead);
  Multiplexer #(.width(8), .enable("false")) multiplexer_2 (
    .in0(Mem[31:24]), .in1(SetData), .out(multiplexer_2_out), .sel(not_2_out));
  or or_3 (or_3_out, WriteEnable3, memRead);
  // Probe on Mem[7:0]
  // Probe on Mem[15:8]
  // Probe on multiplexer_3_out
  Multiplexer #(.width(8), .enable("false")) multiplexer_3 (
    .in0(Mem[7:0]), .in1(SetData), .out(multiplexer_3_out), .sel(not_3_out));
  Register register_1 (.D(multiplexer_3_out), .en(or_1_out), .Q(IineBlocks[7:0]), .clk(CLK));  // open: clr
  not not_4 (not_4_out, memRead);
  Multiplexer #(.width(8), .enable("false")) multiplexer_4 (
    .in0(Mem[15:8]), .in1(SetData), .out(multiplexer_4_out), .sel(not_4_out));
  or or_4 (or_4_out, WriteEnable1, memRead);
  // Probe on IineBlocks[23:16]
  Register register_2 (.D(multiplexer_1_out), .en(or_2_out), .Q(IineBlocks[23:16]), .clk(CLK));  // open: clr
  // Probe on IineBlocks[31:24]
  Register register_3 (.D(multiplexer_2_out), .en(or_3_out), .Q(IineBlocks[31:24]), .clk(CLK));  // open: clr
  // Probe on Mem[23:16]
  // Probe on Mem[31:24]
  // Probe on IineBlocks[7:0]
  // Probe on IineBlocks[15:8]
  Register register_4 (.D(multiplexer_4_out), .en(or_4_out), .Q(IineBlocks[15:8]), .clk(CLK));  // open: clr
  or or_5 (or_5_out, Write2Cache, memRead);
  Register #(.width(7)) State (.D(setTag), .en(or_5_out), .Q(Tag), .clk(CLK));  // open: clr
  // Probe on SetAge
  Demultiplexer #(.select(2)) demultiplexer_1 (
    .out0(WriteEnable0), .out1(WriteEnable1), .out2(WriteEnable2), .out3(WriteEnable3), .in(Write2Cache),
    .sel(offset));  // open: en
  // Probe on offset
  Register #(.width(1)) State_2 (.D(setDirty), .en(or_6_out), .Q(dirty), .clk(CLK));  // open: clr
  or or_6 (or_6_out, memRead, Write2Cache);
  // Probe on Age
  // Probe on offset
  Multiplexer #(.select(2), .width(8), .enable("false")) multiplexer_5 (
    .in0(IineBlocks[7:0]), .in1(IineBlocks[15:8]), .in2(IineBlocks[23:16]), .in3(IineBlocks[31:24]),
    .out(Block), .sel(offset));
  // Probe on Block
  // Probe on updateage_1_nextage
  // Probe on SelectedAge
  UpdateAge updateage_1 (
    .selectAge(SelectedAge), .Age(Age), .initAge(SetAge), .init(init), .clk(CLK),
    .NextAge(updateage_1_nextage));
  or or_7 (or_7_out, UpdateAge, init);
  Register #(.width(2)) State_3 (.D(updateage_1_nextage), .en(or_7_out), .Q(Age), .clk(CLK));  // open: clr
  // Probe on IineBlocks
  // Probe on IineBlocks
  Register #(.width(1)) State_4 (.D(setValid), .en(memRead), .Q(valid), .clk(CLK));  // open: clr
  // Probe on Mem

  // Other names for the same wires on the sheet: MemBlock0[7:0] = Mem[7:0]; MemBlock1[7:0] = Mem[15:8];
  //   MemBlock2[7:0] = Mem[23:16]; MemBlock3[7:0] = Mem[31:24]; Data[7:0] = SetData; block_0[7:0] = IineBlocks[7:0];
  //   block_1[7:0] = IineBlocks[15:8]; block_2[7:0] = IineBlocks[23:16]; block_3[7:0] = IineBlocks[31:24];
  //   initAge[1:0] = SetAge; Tag_t[6:0] = setTag; valid_t = setValid

  // Notes on the sheet:
  //   wrute2cache is from fsm
  //   writeenable0 coimes from saved instruction
  //   get rid of memread
endmodule

module Set (
  input  [6:0] Tag,
  input  clk,
  input  [1:0] offset,
  input  Setvalid,
  input  [7:0] Data,
  input  updateAge,
  input  SetDirty,
  input  init,
  input  memRead,
  input  ByteWrite,
  input  [31:0] MemLine,
  output contains,
  output [7:0] Data_2,
  output dirty,
  output [31:0] lineBlocks,
  output [6:0] TagOut
);

  wire A, B, bytewrite0, bytewrite1, bytewrite2, comparator_3_eq, comparator_4_eq, comparator_5_eq,
       demultiplexer_1_out3, demultiplexer_4_out3, dirty0, dirty1, dirty2, memRead0, memRead1, memRead2,
       setDirty0, setDirty1, setDirty2, setValid0, setValid1, setValid2, valid0, valid1, valid2;
  wire [1:0] Age0, Age1, Age2, line_hit, LRU, multiplexer_1_out, multiplexer_2_out, multiplexer_3_out,
       multiplexer_5_out, multiplexer_6_out, multiplexer_7_out, multiplexer_8_out, SelectedAge;
  wire [2:0] and_1_out;
  wire [6:0] Tag0, Tag1, Tag2;
  wire [7:0] block0, block1, block2, undriven;
  wire [31:0] lineBlocks0, lineBlocks1, lineBlocks2;

  // Probe on Data
  Demultiplexer #(.select(2), .enable("false")) demultiplexer_1 (
    .out0(bytewrite0), .out1(bytewrite1), .out2(bytewrite2), .out3(demultiplexer_1_out3), .in(ByteWrite),
    .sel(multiplexer_1_out));
  Multiplexer #(.width(2), .enable("false")) multiplexer_1 (
    .in0(LRU), .in1(line_hit), .out(multiplexer_1_out), .sel(contains));
  // Probe on 2'b00
  // Probe on multiplexer_1_out
  // Probe on MemLine
  // Probe on Age0
  Line Line0 (
    .setTag(Tag), .setDirty(setDirty0), .UpdateAge(updateAge), .setValid(setValid0), .offset(offset),
    .CLK(clk), .Block(block0), .Tag(Tag0), .Age(Age0), .dirty(dirty0), .valid(valid0), .SetData(Data),
    .init(init), .SetAge(2'b00), .IineBlocks(lineBlocks0), .Mem(MemLine), .memRead(memRead0),
    .Write2Cache(bytewrite0), .SelectedAge(SelectedAge));
  Multiplexer #(.width(2), .enable("false")) multiplexer_2 (.in0(Age0), .in1(Age1), .out(multiplexer_2_out), .sel(A));
  Comparator #(.width(2), .mode("unsigned")) comparator_1 (.a(Age0), .b(Age1), .lt(A));  // open: gt, eq
  Comparator #(.width(2), .mode("unsigned")) comparator_2 (.a(multiplexer_2_out), .b(Age2), .lt(B));  // open: gt, eq
  Demultiplexer #(.select(2), .enable("false")) demultiplexer_2 (
    .out0(memRead0), .out1(memRead1), .out2(memRead2), .in(memRead), .sel(multiplexer_3_out));  // open: out3
  Multiplexer #(.width(2), .enable("false")) multiplexer_3 (
    .in0(LRU), .in1(line_hit), .out(multiplexer_3_out), .sel(contains));
  // Probe on 2'b01
  Line Line1 (
    .setTag(Tag), .setDirty(setDirty1), .UpdateAge(updateAge), .setValid(setValid1), .offset(offset),
    .CLK(clk), .Block(block1), .Tag(Tag1), .Age(Age1), .dirty(dirty1), .valid(valid1), .SetData(Data),
    .init(init), .SetAge(2'b01), .IineBlocks(lineBlocks1), .Mem(MemLine), .memRead(memRead1),
    .Write2Cache(bytewrite1), .SelectedAge(SelectedAge));
  // Probe on Age0
  Multiplexer #(.select(2), .width(2), .enable("false")) multiplexer_4 (
    .in0(Age0), .in1(Age1), .in2(Age2), .out(SelectedAge), .sel(multiplexer_5_out));  // open: in3
  // Probe on Age2
  Multiplexer #(.width(2), .enable("false")) multiplexer_5 (
    .in0(LRU), .in1(line_hit), .out(multiplexer_5_out), .sel(contains));
  Demultiplexer #(.select(2), .enable("false")) demultiplexer_3 (
    .out0(setDirty0), .out1(setDirty1), .out2(setDirty2), .in(SetDirty), .sel(multiplexer_6_out));  // open: out3
  // Probe on Age1
  // Probe on SelectedAge
  Multiplexer #(.width(2), .enable("false")) multiplexer_6 (
    .in0(LRU), .in1(line_hit), .out(multiplexer_6_out), .sel(contains));
  Multiplexer #(.width(2), .enable("false")) multiplexer_7 (
    .in0(LRU), .in1(line_hit), .out(multiplexer_7_out), .sel(contains));
  Demultiplexer #(.select(2), .enable("false")) demultiplexer_4 (
    .out0(setValid0), .out1(setValid1), .out2(setValid2), .out3(demultiplexer_4_out3), .in(Setvalid),
    .sel(multiplexer_8_out));
  Multiplexer #(.width(2), .enable("false")) multiplexer_8 (
    .in0(LRU), .in1(line_hit), .out(multiplexer_8_out), .sel(contains));
  Line Line2 (
    .setTag(Tag), .setDirty(setDirty2), .UpdateAge(updateAge), .setValid(setValid2), .offset(offset),
    .CLK(clk), .Block(block2), .Tag(Tag2), .Age(Age2), .dirty(dirty2), .valid(valid2), .SetData(Data),
    .init(init), .SetAge(2'b10), .IineBlocks(lineBlocks2), .Mem(MemLine), .memRead(memRead2),
    .Write2Cache(bytewrite2), .SelectedAge(SelectedAge));
  Multiplexer #(.select(2), .enable("false")) multiplexer_9 (
    .in0(dirty0), .in1(dirty1), .in2(dirty2), .out(dirty), .sel(multiplexer_7_out));  // open: in3
  // Probe on Tag0
  // Probe on Tag1
  // Probe on Tag2
  // Probe on Tag
  Comparator #(.width(7), .mode("unsigned")) comparator_3 (.a(Tag), .b(Tag0), .eq(comparator_3_eq));  // open: gt, lt
  Comparator #(.width(7), .mode("unsigned")) comparator_4 (.a(Tag), .b(Tag1), .eq(comparator_4_eq));  // open: gt, lt
  Comparator #(.width(7), .mode("unsigned")) comparator_5 (.a(Tag), .b(Tag2), .eq(comparator_5_eq));  // open: gt, lt
  Multiplexer #(.select(2), .width(7), .enable("false")) multiplexer_10 (
    .in0(Tag0), .in1(Tag1), .in2(Tag2), .out(TagOut), .sel(LRU));  // open: in3
  // Probe on LRU
  Multiplexer #(.select(2), .width(2), .enable("false")) multiplexer_11 (
    .in0(2'b00), .in1(2'b01), .in2(2'b10), .in3(2'b10), .out(LRU), .sel({B, A}));
  and and_1 (and_1_out[0], comparator_3_eq, valid0);
  // Probe on valid0
  and and_2 (and_1_out[1], comparator_4_eq, valid1);
  // Probe on valid1
  and and_3 (and_1_out[2], comparator_5_eq, valid2);
  // Probe on valid2
  BitFinder #(.width(3)) bitfinder_1 (.in(and_1_out), .index(line_hit), .found(contains));
  or or_1 (contains, and_1_out[0], and_1_out[1], and_1_out[2]);
  // Probe on line_hit
  // Probe on lineBlocks0
  // Probe on lineBlocks2
  Multiplexer #(.select(2), .width(8), .enable("false")) multiplexer_12 (
    .in0(block0), .in1(block1), .in2(block2), .in3(undriven), .out(Data_2), .sel(line_hit));
  // Probe on lineBlocks
  // Probe on LRU
  Multiplexer #(.select(2), .width(32), .enable("false")) multiplexer_13 (
    .in0(lineBlocks0), .in1(lineBlocks1), .in2(lineBlocks2), .out(lineBlocks), .sel(LRU));  // open: in3
  // also tied to GND on the sheet: {demultiplexer_1_out3, demultiplexer_4_out3}

  // Other names for the same wires on the sheet: SelectedDirty = dirty

  // Notes on the sheet:
  //   Enable for writing
endmodule

module UpdateAge (
  input  [1:0] selectAge,
  input  [1:0] Age,
  input  [1:0] initAge,
  input  init,
  input  clk,
  output [1:0] NextAge
);

  wire comparator_1_eq, comparator_1_lt;
  wire [1:0] adder_1_out, multiplexer_1_out, multiplexer_2_out;

  // Probe on initAge
  // Probe on selectAge
  // Probe on Age
  Comparator #(.width(2), .mode("unsigned")) comparator_1 (
    .a(Age), .b(selectAge), .eq(comparator_1_eq), .lt(comparator_1_lt));  // open: gt
  Adder #(.width(2)) adder_1 (.a(Age), .b(2'b01), .out(adder_1_out));  // open: cin, cout
  Multiplexer #(.width(2), .enable("false")) multiplexer_1 (
    .in0(Age), .in1(adder_1_out), .out(multiplexer_1_out), .sel(comparator_1_lt));
  // Probe on multiplexer_2_out
  Multiplexer #(.width(2), .enable("false")) multiplexer_2 (
    .in0(multiplexer_1_out), .in1(2'b00), .out(multiplexer_2_out), .sel(comparator_1_eq));
  Multiplexer #(.width(2), .enable("false")) multiplexer_3 (
    .in0(multiplexer_2_out), .in1(initAge), .out(NextAge), .sel(init));
  // Probe on initAge
  // Probe on NextAge

  // Other names for the same wires on the sheet: selectedAge[1:0] = selectAge
endmodule

module fsm_controls (
  input  CLK,
  input  read,
  input  write,
  input  contains,
  input  dirty,
  output ready,
  output setDirty,
  output valid,
  output UpdateAge,
  output memRead,
  output memWrite,
  output byteWrite,
  output init,
  output SaveInputs
);

  wire A, and_1_out, and_2_out, and_3_out, and_4_out, and_5_out, and_6_out, and_7_out, and_8_out, and_9_out,
       and_10_out, and_11_out, and_12_out, and_13_out, and_14_out, B, C, not_1_out, not_2_out, not_3_out,
       not_4_out, not_5_out, not_6_out, not_7_out, not_8_out, not_9_out, not_10_out, not_11_out, not_12_out,
       not_13_out, not_14_out, not_15_out, not_16_out, not_17_out, not_18_out, not_19_out, not_20_out,
       not_21_out, not_22_out, not_23_out, not_24_out, not_25_out, not_26_out, not_27_out, not_28_out,
       not_29_out, not_30_out, not_31_out, not_32_out, or_1_out, or_2_out, or_3_out;

  not not_1 (not_1_out, A);
  not not_2 (not_2_out, C);
  not not_3 (not_3_out, contains);
  not not_4 (not_4_out, read);
  not not_5 (not_5_out, A);
  not not_6 (not_6_out, B);
  not not_7 (not_7_out, A);
  not not_8 (not_8_out, read);
  not not_9 (not_9_out, A);
  not not_10 (not_10_out, C);
  not not_11 (not_11_out, B);
  not not_12 (not_12_out, C);
  not not_13 (not_13_out, B);
  not not_14 (not_14_out, C);
  not not_15 (not_15_out, C);
  not not_16 (not_16_out, C);
  not not_17 (not_17_out, write);
  not not_18 (not_18_out, A);
  not not_19 (not_19_out, B);
  not not_20 (not_20_out, C);
  not not_21 (not_21_out, B);
  not not_22 (not_22_out, C);
  not not_23 (not_23_out, A);
  not not_24 (not_24_out, B);
  not not_25 (not_25_out, C);
  not not_26 (not_26_out, B);
  not not_27 (not_27_out, C);
  not not_28 (not_28_out, A);
  not not_29 (not_29_out, B);
  not not_30 (not_30_out, C);
  not not_31 (not_31_out, A);
  not not_32 (not_32_out, C);
  and and_1 (and_1_out, not_1_out, B, not_2_out, not_3_out);
  and and_2 (and_2_out, B, C, not_4_out, write);
  and and_3 (and_3_out, A, C);
  and and_4 (and_4_out, not_5_out, not_6_out, C);
  and and_5 (and_5_out, not_7_out, C, not_8_out);
  and and_6 (and_6_out, not_9_out, B, not_10_out, contains);
  and and_7 (and_7_out, B, C, write);
  and and_8 (and_8_out, A, not_11_out, not_12_out);
  and and_9 (and_9_out, not_13_out, not_14_out);
  and and_10 (and_10_out, not_15_out, dirty);
  and and_11 (and_11_out, not_16_out, contains);
  and and_12 (and_12_out, B, C, not_17_out);
  and and_13 (and_13_out, B, C, read);
  and and_14 (and_14_out, A, B);
  and and_15 (ready, not_18_out, not_19_out, C);
  and and_16 (setDirty, A, B, not_20_out);
  and and_17 (valid, A, not_21_out, not_22_out);
  and and_18 (UpdateAge, not_23_out, B, C);
  and and_19 (memRead, A, not_24_out, not_25_out);
  and and_20 (memWrite, A, not_26_out, C);
  and and_21 (byteWrite, A, B, not_27_out);
  and and_22 (init, not_28_out, not_29_out, not_30_out);
  and and_23 (SaveInputs, not_31_out, B, not_32_out);
  or or_1 (or_1_out, and_1_out, and_2_out, and_3_out);
  or or_2 (or_2_out, and_4_out, and_5_out, and_6_out, and_7_out, and_8_out);
  or or_3 (or_3_out, and_9_out, and_10_out, and_11_out, and_12_out, and_13_out, and_14_out);
  Register #(.width(1)) State (.D(or_1_out), .Q(A), .clk(CLK));  // open: en, clr
  Register #(.width(1)) State_2 (.D(or_2_out), .Q(B), .clk(CLK));  // open: en, clr
  Register #(.width(1)) State_3 (.D(or_3_out), .Q(C), .clk(CLK));  // open: en, clr
endmodule
