// Logisim project 4BitParity.circ as structural Verilog: 5 circuits, main circuit main
module main (
  input  Halt_Enable
);

  wire and_2_out, CLK, Correct, Done_Testing, Halt, Input, not_1_out, not_2_out, not_3_out, Solution,
       YourAnswer;
  wire [6:0] counter_1_q, TestNumber;

  not not_1 (not_1_out, Correct);
  Clock clock_1 (.out(CLK));
  and and_1 (Halt, Halt_Enable, not_1_out);
  Inputs inputs_1 (.Halt(Halt), .CLK(CLK), .Input(Input), .TestNumber(TestNumber), .Done_Testing(Done_Testing));
  _4BitEvenParity u_4bitevenparity_1 (.Input(Input), .CLK(CLK), .Is_Even(YourAnswer));
  // Probe on Input
  // Probe on YourAnswer
  // Probe on Solution
  // Probe on Correct
  not not_2 (not_2_out, Halt);
  and and_2 (and_2_out, Correct, not_2_out, not_3_out);
  not not_3 (not_3_out, Done_Testing);
  Checker checker_1 (.Your_Answer(YourAnswer), .TestNumber(TestNumber), .Correct(Correct), .Solution(Solution));
  Counter #(.width(7), .max('h41), .ongoal("stay")) counter_1 (
    .count(and_2_out), .Q(counter_1_q), .clk(CLK));  // open: load, D, carry, clr
  // Probe on counter_1_q

  // Notes on the sheet:
  //   Max 65
endmodule

module _4BitEvenParity (
  input  Input,
  input  CLK,
  output Is_Even
);

  wire not_1_out, not_2_out;
  wire [3:0] circuit_res, n4bitsubcircuit_1_fact_2_prime;

  _4bitSubCircuit u_4bitsubcircuit_1 (
    .fact_3(circuit_res[3]), .fact_2(circuit_res[2]), .fact_1(circuit_res[1]), .fact_0(circuit_res[0]),
    .Input(Input), .fact_1_prime(n4bitsubcircuit_1_fact_2_prime[3]),
    .fact_0_prime(n4bitsubcircuit_1_fact_2_prime[2]), .fact_3_prime(n4bitsubcircuit_1_fact_2_prime[1]),
    .fact_2_prime(n4bitsubcircuit_1_fact_2_prime[0]));
  not not_1 (not_1_out, circuit_res[2]);
  not not_2 (not_2_out, circuit_res[1]);
  Register #(.width(4)) register_1 (.D(n4bitsubcircuit_1_fact_2_prime), .Q(circuit_res), .clk(CLK));  // open: en, clr
  and and_1 (Is_Even, circuit_res[3], not_1_out, not_2_out, circuit_res[0]);
  // Probe on circuit_res
endmodule

module Inputs (
  input  Halt,
  input  CLK,
  output Input,
  output [6:0] TestNumber,
  output Done_Testing
);

  wire not_1_out;

  not not_1 (not_1_out, Halt);
  Counter #(.width(7), .max('h41), .ongoal("stay")) counter_1 (
    .count(not_1_out), .Q(TestNumber), .carry(Done_Testing), .clk(CLK));  // open: load, D, clr
  ROM #(.addrWidth(7), .dataWidth(1)) rom_1 (.addr(TestNumber), .data(Input));  // open: sel

  // Notes on the sheet:
  //   contents of rom_1 (hex, n*v repeats v):
  //   7*0 1 0 0 1 0 0 0 1 1 0 1 0 0 0 1 0 1 0 1 1 0 0 4*1 0 0 0 1 0 0 1 1 0 1 0 1 0 4*1 0 0 1 1 0 4*1 0
  //   4*1
endmodule

module Checker (
  input  Your_Answer,
  input  [6:0] TestNumber,
  output Correct,
  output Solution
);

  ROM #(.addrWidth(7), .dataWidth(1)) rom_1 (.addr(TestNumber), .data(Solution));  // open: sel
  Comparator #(.width(1)) comparator_1 (.a(Solution), .b(Your_Answer), .eq(Correct));  // open: gt, lt

  // Notes on the sheet:
  //   contents of rom_1 (hex, n*v repeats v):
  //   4*0 1 11*0 1 7*0 1 0 0 0 1 11*0 1 0 0 0 1 7*0 1 11*0 1
endmodule

module _4bitSubCircuit (
  input  fact_3,
  input  fact_2,
  input  fact_1,
  input  fact_0,
  input  Input,
  output fact_1_prime,
  output fact_0_prime,
  output fact_3_prime,
  output fact_2_prime
);

  wire and_1_out, and_2_out, and_3_out, and_4_out, and_5_out, and_6_out, and_7_out, and_8_out, and_9_out,
       and_10_out, and_11_out, and_12_out, and_13_out, and_14_out, and_15_out, and_16_out, and_17_out,
       and_18_out, and_19_out, not_1_out, not_2_out, not_3_out, not_4_out, not_5_out, not_6_out, not_7_out,
       not_8_out, not_9_out, not_10_out, not_11_out, not_12_out, not_13_out, not_14_out, not_15_out,
       not_16_out, not_17_out, not_18_out, not_20_out, not_21_out, not_22_out, not_23_out;

  not not_1 (not_1_out, fact_3);
  not not_2 (not_2_out, fact_2);
  not not_3 (not_3_out, fact_3);
  not not_4 (not_4_out, fact_2);
  not not_5 (not_5_out, fact_3);
  not not_6 (not_6_out, fact_3);
  not not_7 (not_7_out, Input);
  not not_8 (not_8_out, fact_0);
  and and_1 (and_1_out, not_1_out, not_2_out, Input);
  and and_2 (and_2_out, not_3_out, not_4_out, fact_0);
  and and_3 (and_3_out, not_5_out, fact_0, Input);
  and and_4 (and_4_out, fact_1, Input);
  and and_5 (and_5_out, not_6_out, fact_2, not_7_out);
  and and_6 (and_6_out, fact_2, not_8_out, Input);
  and and_7 (and_7_out, fact_2, fact_1);
  not not_9 (not_9_out, fact_3);
  not not_10 (not_10_out, fact_3);
  not not_11 (not_11_out, Input);
  not not_12 (not_12_out, Input);
  not not_13 (not_13_out, fact_0);
  not not_14 (not_14_out, fact_1);
  not not_15 (not_15_out, fact_0);
  and and_8 (and_8_out, not_9_out, not_10_out, Input);
  and and_9 (and_9_out, fact_0, not_11_out);
  and and_10 (and_10_out, fact_1, not_12_out);
  and and_11 (and_11_out, fact_2, not_13_out, Input);
  and and_12 (and_12_out, fact_2, fact_1);
  and and_13 (and_13_out, fact_3, not_14_out, not_15_out, Input);
  or or_1 (fact_2_prime, and_1_out, and_2_out, and_3_out, and_4_out, and_5_out, and_6_out, and_7_out);
  or or_2 (fact_0_prime, and_8_out, and_9_out, and_10_out, and_11_out, and_12_out, and_13_out);
  not not_16 (not_16_out, fact_2);
  not not_17 (not_17_out, fact_1);
  not not_18 (not_18_out, fact_0);
  not not_19 (not_18_out, Input);
  not not_20 (not_20_out, fact_3);
  not not_21 (not_21_out, Input);
  not not_22 (not_22_out, fact_1);
  not not_23 (not_23_out, fact_0);
  and and_14 (and_14_out, fact_3, not_16_out, not_17_out, not_18_out, not_18_out);
  and and_15 (and_15_out, fact_3, fact_2, fact_0, Input);
  and and_16 (and_16_out, not_20_out, fact_0, Input);
  and and_17 (and_17_out, fact_2, not_21_out);
  and and_18 (and_18_out, fact_2, fact_0);
  and and_19 (and_19_out, fact_3, not_22_out, not_23_out);
  or or_3 (fact_1_prime, and_14_out, and_15_out);
  or or_4 (fact_3_prime, and_16_out, and_17_out, and_18_out, and_19_out);

  // Other names for the same wires on the sheet: B0 = fact_0; B1 = fact_1; B2 = fact_2; B3 = fact_3
endmodule
