// Logisim project CPU.circ as structural Verilog: 12 circuits, main circuit CPU
module CPU (
);

  wire CLK, decoding_circ_1_out_5, decoding_circ_1_output2, decoding_circ_1_output3, not_1_out;
  wire [3:0] bit1, decoding_circ_1_output1, main_alu_circ_1_result, multiplexer_1_out, reg_file_1_a_data,
       reg_file_1_b_data;
  wire [4:0] counter_1_q;
  wire [15:4] rom_1_data;

  Clock clock_1 (.out(CLK));
  not not_1 (not_1_out, decoding_circ_1_out_5);
  Counter #(.width(5), .max('h1f)) counter_1 (
    .count(not_1_out), .Q(counter_1_q), .clk(CLK));  // open: load, D, carry, clr
  Decoding_circ decoding_circ_1 (
    .OpCode(rom_1_data[15:12]), .output1(decoding_circ_1_output1), .output2(decoding_circ_1_output2),
    .output3(decoding_circ_1_output3), .out_5(decoding_circ_1_out_5));
  ROM #(.addrWidth(5), .dataWidth(16)) rom_1 (.addr(counter_1_q), .data({rom_1_data, bit1}));  // open: sel
  Reg_File reg_file_1 (
    .A(rom_1_data[7:4]), .B(bit1), .C(rom_1_data[11:8]), .Data_In(main_alu_circ_1_result),
    .Reg_Write(decoding_circ_1_output2), .CLK(CLK), .A_DATA(reg_file_1_a_data), .B_DATA(reg_file_1_b_data));
  main_alu_circ main_alu_circ_1 (
    ._1st(decoding_circ_1_output1), ._2nd(reg_file_1_a_data), ._3rd(multiplexer_1_out),
    .result(main_alu_circ_1_result));
  Multiplexer #(.width(4), .enable("false")) multiplexer_1 (
    .in0(reg_file_1_b_data), .in1(bit1), .out(multiplexer_1_out), .sel(decoding_circ_1_output3));

  // Notes on the sheet:
  //   Instructions
  //   contents of rom_1 (hex, n*v repeats v):
  //   2003 2106 1005 3210 4301 5433 6520 763c 8720 986f b938 ca77 db13 ec62 fd85 e05
endmodule

module Decoding_circ (
  input  [3:0] OpCode,
  output [3:0] output1,
  output output2,
  output output3,
  output out_5
);

  subCirc_p subcirc_p_1 (
    .d(OpCode[3]), .c(OpCode[2]), .b(OpCode[1]), .a(OpCode[0]), .output3(output1[3]), .output2(output1[2]),
    .output1(output1[1]), .output0(output1[0]));
  subCirc_i subcirc_i_1 (.d(OpCode[3]), .c(OpCode[2]), .b(OpCode[1]), .a(OpCode[0]), .\output (output3));
  Comparator #(.width(4)) comparator_1 (.a(OpCode), .b(4'b0000), .eq(out_5));  // open: gt, lt
  subCirc_e subcirc_e_1 (.d(OpCode[3]), .c(OpCode[2]), .b(OpCode[1]), .a(OpCode[0]), .\output (output2));
endmodule

module main_alu_circ (
  input  [3:0] _1st,
  input  [3:0] _2nd,
  input  [3:0] _3rd,
  output [3:0] result
);

  wire [3:0] after_addition, and_circ_1_and_output, B_with4bits_not, multiplexer_1_out,
       negation_circ_1_negation_output, not_circ_1_not_output, or_circ_1_or_output, xor_circ_1_xor_output;

  assign B_with4bits_not = ~_3rd;  // NOT_Gate not_1, 4 bits wide
  Adder #(.width(4)) adder_1 (.a(_2nd), .b(multiplexer_1_out), .out(after_addition), .cin(_1st[3]));  // open: cout
  Multiplexer #(.width(4), .enable("false")) multiplexer_1 (
    .in0(_3rd), .in1(B_with4bits_not), .out(multiplexer_1_out), .sel(_1st[3]));
  And_circ and_circ_1 (._2nd(_2nd), ._3rd(_3rd), .AND_output(and_circ_1_and_output));
  Or_circ or_circ_1 (._2nd(_2nd), ._3rd(_3rd), .OR_output(or_circ_1_or_output));
  Xor_circ xor_circ_1 (._2nd(_2nd), ._3rd(_3rd), .XOR_output(xor_circ_1_xor_output));
  NOt_circ not_circ_1 (._2nd(_2nd), .NOT_output(not_circ_1_not_output));
  Negation_circ negation_circ_1 (._2nd(_2nd), .Negation_output(negation_circ_1_negation_output));
  Multiplexer #(.select(3), .width(4), .enable("false")) multiplexer_2 (
    .in0(_3rd), .in1(_2nd), .in2(and_circ_1_and_output), .in3(or_circ_1_or_output),
    .in4(xor_circ_1_xor_output), .in5(not_circ_1_not_output), .in6(negation_circ_1_negation_output),
    .in7(after_addition), .out(result), .sel(_1st[2:0]));

  // Other names for the same wires on the sheet: _4_bits[3:0] = _1st; A_with4bits[3:0] = _2nd;
  //   B_with4bits[3:0] = _3rd
endmodule

module Reg_File (
  input  [3:0] A,
  input  [3:0] B,
  input  [3:0] C,
  input  [3:0] Data_In,
  input  Reg_Write,
  input  CLK,
  output [3:0] A_DATA,
  output [3:0] B_DATA
);

  wire Write_Reg0, Write_Reg1, Write_Reg2, Write_Reg3, Write_Reg4, Write_Reg5, Write_Reg6, Write_Reg7,
       Write_Reg8, Write_Reg9, Write_Reg10, Write_Reg11, Write_Reg12, Write_Reg13, Write_Reg14, Write_Reg15;
  wire [3:0] Reg0, Reg1, Reg2, Reg3, Reg4, Reg5, Reg6, Reg7, Reg8, Reg9, Reg10, Reg11, Reg12, Reg13, Reg14,
       Reg15;

  Demultiplexer #(.select(4), .enable("false")) demultiplexer_1 (
    .out0(Write_Reg0), .out1(Write_Reg1), .out2(Write_Reg2), .out3(Write_Reg3), .out4(Write_Reg4),
    .out5(Write_Reg5), .out6(Write_Reg6), .out7(Write_Reg7), .out8(Write_Reg8), .out9(Write_Reg9),
    .out10(Write_Reg10), .out11(Write_Reg11), .out12(Write_Reg12), .out13(Write_Reg13), .out14(Write_Reg14),
    .out15(Write_Reg15), .in(Reg_Write), .sel(C));
  // Probe on Reg0
  Register #(.width(4)) u_Reg0 (.D(Data_In), .en(Write_Reg0), .Q(Reg0), .clk(CLK));  // open: clr
  // Probe on Reg4
  Register #(.width(4)) u_Reg4 (.D(Data_In), .en(Write_Reg4), .Q(Reg4), .clk(CLK));  // open: clr
  // Probe on Reg8
  Register #(.width(4)) u_Reg8 (.D(Data_In), .en(Write_Reg8), .Q(Reg8), .clk(CLK));  // open: clr
  // Probe on Reg12
  Register #(.width(4)) u_Reg12 (.D(Data_In), .en(Write_Reg12), .Q(Reg12), .clk(CLK));  // open: clr
  // Probe on Reg1
  Register #(.width(4)) u_Reg1 (.D(Data_In), .en(Write_Reg1), .Q(Reg1), .clk(CLK));  // open: clr
  // Probe on Reg5
  Register #(.width(4)) u_Reg5 (.D(Data_In), .en(Write_Reg5), .Q(Reg5), .clk(CLK));  // open: clr
  // Probe on Reg9
  Register #(.width(4)) u_Reg9 (.D(Data_In), .en(Write_Reg9), .Q(Reg9), .clk(CLK));  // open: clr
  // Probe on Reg13
  Register #(.width(4)) u_Reg13 (.D(Data_In), .en(Write_Reg13), .Q(Reg13), .clk(CLK));  // open: clr
  Register #(.width(4)) u_Reg2 (.D(Data_In), .en(Write_Reg2), .Q(Reg2), .clk(CLK));  // open: clr
  Register #(.width(4)) u_Reg6 (.D(Data_In), .en(Write_Reg6), .Q(Reg6), .clk(CLK));  // open: clr
  Register #(.width(4)) u_Reg10 (.D(Data_In), .en(Write_Reg10), .Q(Reg10), .clk(CLK));  // open: clr
  Register #(.width(4)) u_Reg14 (.D(Data_In), .en(Write_Reg14), .Q(Reg14), .clk(CLK));  // open: clr
  // Probe on Reg2
  // Probe on Reg6
  // Probe on Reg10
  // Probe on Reg14
  // Probe on Reg3
  Register #(.width(4)) u_Reg3 (.D(Data_In), .en(Write_Reg3), .Q(Reg3), .clk(CLK));  // open: clr
  // Probe on Reg7
  Register #(.width(4)) u_Reg7 (.D(Data_In), .en(Write_Reg7), .Q(Reg7), .clk(CLK));  // open: clr
  // Probe on Reg11
  Register #(.width(4)) u_Reg11 (.D(Data_In), .en(Write_Reg11), .Q(Reg11), .clk(CLK));  // open: clr
  // Probe on Reg15
  Register #(.width(4)) u_Reg15 (.D(Data_In), .en(Write_Reg15), .Q(Reg15), .clk(CLK));  // open: clr
  Multiplexer #(.select(4), .width(4), .enable("false")) multiplexer_1 (
    .in0(Reg0), .in1(Reg1), .in2(Reg2), .in3(Reg3), .in4(Reg4), .in5(Reg5), .in6(Reg6), .in7(Reg7),
    .in8(Reg8), .in9(Reg9), .in10(Reg10), .in11(Reg11), .in12(Reg12), .in13(Reg13), .in14(Reg14),
    .in15(Reg15), .out(A_DATA), .sel(A));
  Multiplexer #(.select(4), .width(4), .enable("false")) multiplexer_2 (
    .in0(Reg0), .in1(Reg1), .in2(Reg2), .in3(Reg3), .in4(Reg4), .in5(Reg5), .in6(Reg6), .in7(Reg7),
    .in8(Reg8), .in9(Reg9), .in10(Reg10), .in11(Reg11), .in12(Reg12), .in13(Reg13), .in14(Reg14),
    .in15(Reg15), .out(B_DATA), .sel(B));
endmodule

module subCirc_p (
  input  d,
  input  c,
  input  b,
  input  a,
  output output3,
  output output2,
  output output1,
  output output0
);

  wire and_2_out, and_3_out, and_4_out, and_5_out, and_6_out, bit_a_not, bit_b_not, bit_c_not, bit_d_not;

  and and_1 (output3, d, c, b);
  and and_2 (and_2_out, d, b, a);
  and and_3 (and_3_out, bit_d_not, bit_c_not, a);
  and and_4 (and_4_out, c, b);
  and and_5 (and_5_out, d, b, bit_a_not);
  and and_6 (and_6_out, d, c);
  assign {bit_a_not, bit_b_not, bit_c_not, bit_d_not} = ~{a, b, c, d};  // NOT_Gate not_1, 4 bits wide
  or or_1 (output1, c, and_2_out);
  or or_2 (output0, and_3_out, and_4_out, and_5_out, and_6_out);

  assign output2 = d;

  // Other names for the same wires on the sheet: bit_d = d; bit_c = c; bit_b = b; bit_a = a
endmodule

module subCirc_i (
  input  d,
  input  c,
  input  b,
  input  a,
  output \output 
);

  wire and_1_out, and_2_out, and_3_out, bit__not_a, bit__not_b, bit__not_c, bit__not_d;

  and and_1 (and_1_out, a, bit__not_b);
  and and_2 (and_2_out, bit__not_d, bit__not_c, bit__not_a);
  and and_3 (and_3_out, c, a);
  assign {bit__not_a, bit__not_b, bit__not_c, bit__not_d} = ~{a, b, c, d};  // NOT_Gate not_1, 4 bits wide
  or or_1 (\output , and_1_out, and_2_out, and_3_out);

  // Other names for the same wires on the sheet: bit_d = d; bit_c = c; bit_b = b; bit_a = a

  // Notes on the sheet:
  //   d: pull=up
endmodule

module subCirc_e (
  input  d,
  input  c,
  input  b,
  input  a,
  output \output 
);

  or or_1 (\output , d, c, b);
endmodule

module And_circ (
  input  [3:0] _2nd,
  input  [3:0] _3rd,
  output [3:0] AND_output
);

  assign AND_output = _2nd & _3rd;  // AND_Gate and_1, 4 bits wide

  // Other names for the same wires on the sheet: A_with4bits[3:0] = _2nd; B_with4bits[3:0] = _3rd
endmodule

module Or_circ (
  input  [3:0] _2nd,
  input  [3:0] _3rd,
  output [3:0] OR_output
);

  assign OR_output = _2nd | _3rd;  // OR_Gate or_1, 4 bits wide

  // Other names for the same wires on the sheet: A_with4bits[3:0] = _2nd; B_with4bits[3:0] = _3rd
endmodule

module Xor_circ (
  input  [3:0] _2nd,
  input  [3:0] _3rd,
  output [3:0] XOR_output
);

  assign XOR_output = _2nd ^ _3rd;  // XOR_Gate xor_1, 4 bits wide

  // Other names for the same wires on the sheet: A_with4bits[3:0] = _2nd; B_with4bits[3:0] = _3rd
endmodule

module NOt_circ (
  input  [3:0] _2nd,
  output [3:0] NOT_output
);

  assign NOT_output = ~_2nd;  // NOT_Gate not_1, 4 bits wide

  // Other names for the same wires on the sheet: A_with4bits[3:0] = _2nd
endmodule

module Negation_circ (
  input  [3:0] _2nd,
  output [3:0] Negation_output
);

  Negator #(.width(4)) negator_1 (.in(_2nd), .out(Negation_output));

  // Other names for the same wires on the sheet: A_with4bits[3:0] = _2nd
endmodule
