// Logisim project CPU.circ as structural Verilog: 12 circuits, main circuit CPU
module CPU (
);

  wire circuit_decode_1_out_5, circuit_decode_1_output2, circuit_decode_1_output3, CLK, not_1_out;
  wire [3:0] alu_main_circuit_1_result, bit1, circuit_decode_1_output1, multiplexer_1_out, reg_file_1_a_data,
       reg_file_1_b_data, rom_1_data_2;
  wire [4:0] counter_1_q;
  wire [11:4] rom_1_data;

  Clock clock_1 (.out(CLK));
  not not_1 (not_1_out, circuit_decode_1_out_5);
  Counter #(.width(5), .max('h1f)) counter_1 (
    .count(not_1_out), .Q(counter_1_q), .clk(CLK));  // open: load, D, carry, clr
  Circuit_Decode circuit_decode_1 (
    .OpCode(rom_1_data_2), .output1(circuit_decode_1_output1), .output2(circuit_decode_1_output2),
    .output3(circuit_decode_1_output3), .out_5(circuit_decode_1_out_5));
  ROM #(.addrWidth(5), .dataWidth(16)) rom_1 (
    .addr(counter_1_q), .data({rom_1_data_2, rom_1_data, bit1}));  // open: sel
  Reg_File reg_file_1 (
    .A(rom_1_data[7:4]), .B(bit1), .C(rom_1_data[11:8]), .Data_In(alu_main_circuit_1_result),
    .Reg_Write(circuit_decode_1_output2), .CLK(CLK), .A_DATA(reg_file_1_a_data), .B_DATA(reg_file_1_b_data));
  ALU_Main_Circuit alu_main_circuit_1 (
    ._1st(circuit_decode_1_output1), ._2nd(reg_file_1_a_data), ._3rd(multiplexer_1_out),
    .result(alu_main_circuit_1_result));
  Multiplexer #(.width(4), .enable("false")) multiplexer_1 (
    .in0(reg_file_1_b_data), .in1(bit1), .out(multiplexer_1_out), .sel(circuit_decode_1_output3));

  // Notes on the sheet:
  //   Instructions
  //   contents of rom_1 (hex, n*v repeats v):
  //   2003 2106 1005 3210 4301 5433 6520 763c 8720 986f b938 ca77 db13 ec62 fd85 e05
endmodule

module Circuit_Decode (
  input  [3:0] OpCode,
  output [3:0] output1,
  output output2,
  output output3,
  output out_5
);

  Sub_Circ_A sub_circ_a_1 (
    .a(OpCode[3]), .b(OpCode[2]), .c(OpCode[1]), .d(OpCode[0]), .OutPut3(output1[3]), .OutPut2(output1[2]),
    .OutPut1(output1[1]), .OutPut0(output1[0]));
  Sub_Circuit_C sub_circuit_c_1 (.d(OpCode[3]), .c(OpCode[2]), .b(OpCode[1]), .a(OpCode[0]), .\output (output2));
  Sub_Circuit_B sub_circuit_b_1 (.a(OpCode[3]), .b(OpCode[2]), .c(OpCode[1]), .d(OpCode[0]), .\output (output3));
  Comparator #(.width(4)) comparator_1 (.a(OpCode), .b(4'b0000), .eq(out_5));  // open: gt, lt
endmodule

module ALU_Main_Circuit (
  input  [3:0] _1st,
  input  [3:0] _2nd,
  input  [3:0] _3rd,
  output [3:0] result
);

  wire [3:0] Addition, and_circuit_1_and, Bits4B_NOT, multiplexer_1_out, negate_circuit_1_outputnegation,
       not_circuit_1_not, or_circuit_1_or, xor_circuit_1_xor;

  assign Bits4B_NOT = ~_3rd;  // NOT_Gate not_1, 4 bits wide
  Adder #(.width(4)) adder_1 (.a(_2nd), .b(multiplexer_1_out), .out(Addition), .cin(_1st[3]));  // open: cout
  Multiplexer #(.width(4), .enable("false")) multiplexer_1 (
    .in0(_3rd), .in1(Bits4B_NOT), .out(multiplexer_1_out), .sel(_1st[3]));
  AND_Circuit and_circuit_1 (._2ndINPUT(_2nd), ._3rdINPUT(_3rd), .AND(and_circuit_1_and));
  OR_Circuit or_circuit_1 (._2ndINPUT(_2nd), ._3rdINPUT(_3rd), .OR(or_circuit_1_or));
  XOR_Circuit xor_circuit_1 (._2nd(_2nd), ._3rd(_3rd), .XOR(xor_circuit_1_xor));
  NOT_Circuit not_circuit_1 (._4Bit_A(_2nd), .Not(not_circuit_1_not));
  NEGATE_Circuit negate_circuit_1 (._2nd(_2nd), .OutPutNegation(negate_circuit_1_outputnegation));
  Multiplexer #(.select(3), .width(4), .enable("false")) multiplexer_2 (
    .in0(_3rd), .in1(_2nd), .in2(and_circuit_1_and), .in3(or_circuit_1_or), .in4(xor_circuit_1_xor),
    .in5(not_circuit_1_not), .in6(negate_circuit_1_outputnegation), .in7(Addition), .out(result),
    .sel(_1st[2:0]));

  // Other names for the same wires on the sheet: Bits4[3:0] = _1st; Bits4A[3:0] = _2nd; Bits4B[3:0] = _3rd
endmodule

module Reg_File (
  input  [3:0] A,
  input  [3:0] B,
  input  [3:0] C,
  input  [3:0] Data_In,
  input  Reg_Write,
  input  CLK,
  output [3:0] A_DATA,
  output [3:0] B_DATA
);

  wire Write_Reg0, Write_Reg1, Write_Reg2, Write_Reg3, Write_Reg4, Write_Reg5, Write_Reg6, Write_Reg7,
       Write_Reg8, Write_Reg9, Write_Reg10, Write_Reg11, Write_Reg12, Write_Reg13, Write_Reg14, Write_Reg15;
  wire [3:0] Reg0, Reg1, Reg2, Reg3, Reg4, Reg5, Reg6, Reg7, Reg8, Reg9, Reg10, Reg11, Reg12, Reg13, Reg14,
       Reg15;

  Demultiplexer #(.select(4), .enable("false")) demultiplexer_1 (
    .out0(Write_Reg0), .out1(Write_Reg1), .out2(Write_Reg2), .out3(Write_Reg3), .out4(Write_Reg4),
    .out5(Write_Reg5), .out6(Write_Reg6), .out7(Write_Reg7), .out8(Write_Reg8), .out9(Write_Reg9),
    .out10(Write_Reg10), .out11(Write_Reg11), .out12(Write_Reg12), .out13(Write_Reg13), .out14(Write_Reg14),
    .out15(Write_Reg15), .in(Reg_Write), .sel(C));
  // Probe on Reg0
  Register #(.width(4)) u_Reg0 (.D(Data_In), .en(Write_Reg0), .Q(Reg0), .clk(CLK));  // open: clr
  // Probe on Reg4
  Register #(.width(4)) u_Reg4 (.D(Data_In), .en(Write_Reg4), .Q(Reg4), .clk(CLK));  // open: clr
  // Probe on Reg8
  Register #(.width(4)) u_Reg8 (.D(Data_In), .en(Write_Reg8), .Q(Reg8), .clk(CLK));  // open: clr
  // Probe on Reg12
  Register #(.width(4)) u_Reg12 (.D(Data_In), .en(Write_Reg12), .Q(Reg12), .clk(CLK));  // open: clr
  // Probe on Reg1
  Register #(.width(4)) u_Reg1 (.D(Data_In), .en(Write_Reg1), .Q(Reg1), .clk(CLK));  // open: clr
  // Probe on Reg5
  Register #(.width(4)) u_Reg5 (.D(Data_In), .en(Write_Reg5), .Q(Reg5), .clk(CLK));  // open: clr
  // Probe on Reg9
  Register #(.width(4)) u_Reg9 (.D(Data_In), .en(Write_Reg9), .Q(Reg9), .clk(CLK));  // open: clr
  // Probe on Reg13
  Register #(.width(4)) u_Reg13 (.D(Data_In), .en(Write_Reg13), .Q(Reg13), .clk(CLK));  // open: clr
  Register #(.width(4)) u_Reg2 (.D(Data_In), .en(Write_Reg2), .Q(Reg2), .clk(CLK));  // open: clr
  Register #(.width(4)) u_Reg6 (.D(Data_In), .en(Write_Reg6), .Q(Reg6), .clk(CLK));  // open: clr
  Register #(.width(4)) u_Reg10 (.D(Data_In), .en(Write_Reg10), .Q(Reg10), .clk(CLK));  // open: clr
  Register #(.width(4)) u_Reg14 (.D(Data_In), .en(Write_Reg14), .Q(Reg14), .clk(CLK));  // open: clr
  // Probe on Reg2
  // Probe on Reg6
  // Probe on Reg10
  // Probe on Reg14
  // Probe on Reg3
  Register #(.width(4)) u_Reg3 (.D(Data_In), .en(Write_Reg3), .Q(Reg3), .clk(CLK));  // open: clr
  // Probe on Reg7
  Register #(.width(4)) u_Reg7 (.D(Data_In), .en(Write_Reg7), .Q(Reg7), .clk(CLK));  // open: clr
  // Probe on Reg11
  Register #(.width(4)) u_Reg11 (.D(Data_In), .en(Write_Reg11), .Q(Reg11), .clk(CLK));  // open: clr
  // Probe on Reg15
  Register #(.width(4)) u_Reg15 (.D(Data_In), .en(Write_Reg15), .Q(Reg15), .clk(CLK));  // open: clr
  Multiplexer #(.select(4), .width(4), .enable("false")) multiplexer_1 (
    .in0(Reg0), .in1(Reg1), .in2(Reg2), .in3(Reg3), .in4(Reg4), .in5(Reg5), .in6(Reg6), .in7(Reg7),
    .in8(Reg8), .in9(Reg9), .in10(Reg10), .in11(Reg11), .in12(Reg12), .in13(Reg13), .in14(Reg14),
    .in15(Reg15), .out(A_DATA), .sel(A));
  Multiplexer #(.select(4), .width(4), .enable("false")) multiplexer_2 (
    .in0(Reg0), .in1(Reg1), .in2(Reg2), .in3(Reg3), .in4(Reg4), .in5(Reg5), .in6(Reg6), .in7(Reg7),
    .in8(Reg8), .in9(Reg9), .in10(Reg10), .in11(Reg11), .in12(Reg12), .in13(Reg13), .in14(Reg14),
    .in15(Reg15), .out(B_DATA), .sel(B));
endmodule

module Sub_Circ_A (
  input  a,
  input  b,
  input  c,
  input  d,
  output OutPut3,
  output OutPut2,
  output OutPut1,
  output OutPut0
);

  wire and_2_out, and_3_out, and_4_out, and_5_out, and_6_out, not_1_out, not_2_out, not_3_out;

  and and_1 (OutPut3, b, c, d);
  and and_2 (and_2_out, a, b, d);
  not not_1 (not_1_out, a);
  and and_3 (and_3_out, not_1_out, b, d);
  and and_4 (and_4_out, b, c);
  and and_5 (and_5_out, c, d);
  and and_6 (and_6_out, a, not_2_out, not_3_out);
  not not_2 (not_2_out, c);
  not not_3 (not_3_out, d);
  or or_1 (OutPut1, and_2_out, c);
  or or_2 (OutPut0, and_3_out, and_4_out, and_5_out, and_6_out);

  assign OutPut2 = d;
endmodule

module Sub_Circuit_B (
  input  a,
  input  b,
  input  c,
  input  d,
  output \output 
);

  wire and_1_out, and_2_out, and_3_out, not_1_out, not_2_out, not_3_out, not_4_out;

  not not_1 (not_1_out, b);
  not not_2 (not_2_out, d);
  not not_3 (not_3_out, a);
  not not_4 (not_4_out, c);
  and and_1 (and_1_out, a, c);
  and and_2 (and_2_out, a, not_1_out);
  and and_3 (and_3_out, not_3_out, not_4_out, not_2_out);
  or or_1 (\output , and_1_out, and_2_out, and_3_out);
endmodule

module Sub_Circuit_C (
  input  d,
  input  c,
  input  b,
  input  a,
  output \output 
);

  or or_1 (\output , d, c, b);
endmodule

module AND_Circuit (
  input  [3:0] _2ndINPUT,
  input  [3:0] _3rdINPUT,
  output [3:0] AND
);

  assign AND = _2ndINPUT & _3rdINPUT;  // AND_Gate and_1, 4 bits wide
endmodule

module OR_Circuit (
  input  [3:0] _2ndINPUT,
  input  [3:0] _3rdINPUT,
  output [3:0] OR
);

  assign OR = _2ndINPUT | _3rdINPUT;  // OR_Gate or_1, 4 bits wide
endmodule

module XOR_Circuit (
  input  [3:0] _2nd,
  input  [3:0] _3rd,
  output [3:0] XOR
);

  assign XOR = _2nd ^ _3rd;  // XOR_Gate xor_1, 4 bits wide
endmodule

module NOT_Circuit (
  input  [3:0] _4Bit_A,
  output [3:0] Not
);

  assign Not = ~_4Bit_A;  // NOT_Gate not_1, 4 bits wide
endmodule

module NEGATE_Circuit (
  input  [3:0] _2nd,
  output [3:0] OutPutNegation
);

  Negator #(.width(4)) negator_1 (.in(_2nd), .out(OutPutNegation));
endmodule
